// Logisim project ALU_fixed.circ as structural Verilog: 6 circuits, main circuit ALU
module ALU (
  input  [31:0] in_1,
  input  [31:0] in_2,
  input  [5:0] Func_Code,
  input  [5:0] Op_Code,
  input  [15:0] Constante,
  input  Tipo_de_Instruccion,
  output [31:0] Output,
  output [31:0] Hi,
  output [31:0] LO,
  output L_HI_LO
);

  wire tunnel;
  wire [3:0] Op;
  wire [31:0] B_Constante, multiplexer_1_out;

  Multiplexer #(.width(32)) multiplexer_1 (
    .in0(in_2), .in1(B_Constante), .out(multiplexer_1_out), .sel(Tipo_de_Instruccion));  // open: en
  ALU_Control alu_control_1 (
    .in_1(Func_Code), .in_2(Op_Code), .in_3(Constante), .out_4(tunnel), .Output(B_Constante),
    .L_HI_LO(L_HI_LO), .Selector(Op));
  ALU_Operations alu_operations_1 (
    .in_1(in_1), .Output(Output), .in_2(multiplexer_1_out), .in_3(tunnel), .Hi(Hi), .in_4(Op), .LO(LO));

  // Other names for the same wires on the sheet: A[31:0] = in_1; B[31:0] = in_2; Type_I = Tipo_de_Instruccion
endmodule

module ALU_Operations (
  input  [31:0] in_1,
  input  [31:0] in_2,
  input  in_3,
  input  [3:0] in_4,
  output [31:0] Output,
  output [31:0] Hi,
  output [31:0] LO
);

  wire Sel_Mul;
  wire [31:0] add, \and , Mul_HI, Mul_LO, \nor , \or , Remander, Result, slt_sltu, Sub, \xor ;

  Adder #(.width(32)) adder_1 (.a(in_1), .b(in_2), .out(add));  // open: cin, cout
  Subtractor #(.width(32)) subtractor_1 (.a(in_1), .b(in_2), .out(Sub));  // open: bin, bout
  Multi multi_1 (.in_1(in_1), .HI(Mul_HI), .in_2(in_2), .LO(Mul_LO), .in_3(in_3));
  Divi divi_1 (.out_4(Result), .in_1(in_1), .out_5(Remander), .in_2(in_2), .in_3(in_3));
  assign \and  = in_1 & in_2;  // AND_Gate and_1, 32 bits wide
  assign \or  = in_1 | in_2;  // OR_Gate or_1, 32 bits wide
  assign \xor  = in_1 ^ in_2;  // XOR_Gate xor_1, 32 bits wide
  assign \nor  = ~(in_1 | in_2);  // NOR_Gate nor_1, 32 bits wide
  Comparer comparer_1 (.in_1(in_1), .Output(slt_sltu), .in_2(in_2), .in_3(in_3));
  Comparator #(.width(4)) comparator_1 (.a(in_4), .b(4'b0010), .eq(Sel_Mul));  // open: gt, lt
  Multiplexer #(.select(4), .width(32)) multiplexer_1 (
    .in0(add), .in1(Sub), .in4(\and ), .in5(\or ), .in6(\nor ), .in7(\xor ), .in8(slt_sltu), .out(Output),
    .sel(in_4));  // open: in2, in3, in9, in10, in11, in12, in13, in14, in15, en
  Multiplexer #(.width(32)) multiplexer_2 (.in0(Remander), .in1(Mul_HI), .out(Hi), .sel(Sel_Mul));  // open: en
  Multiplexer #(.width(32)) multiplexer_3 (.in0(Result), .in1(Mul_LO), .out(LO), .sel(Sel_Mul));  // open: en

  // Other names for the same wires on the sheet: A[31:0] = in_1; B[31:0] = in_2; Op[3:0] = in_4; tunnel = in_3

  // Notes on the sheet:
  //   Arithmetics
  //   Logic
  //   COMPARER
endmodule

module ALU_Control (
  input  [5:0] in_1,
  input  [5:0] in_2,
  input  [15:0] in_3,
  output out_4,
  output [31:0] Output,
  output L_HI_LO,
  output [3:0] Selector
);

  wire add, addi, \and , and_13_out, andi, comparator_7_eq, comparator_8_eq, comparator_9_eq,
       comparator_10_eq, comparator_11_eq, comparator_12_eq, comparator_13_eq, comparator_14_eq,
       comparator_15_eq, comparator_16_eq, comparator_17_eq, comparator_18_eq, comparator_19_eq, div, divu,
       mult, mulu, \nor , \or , ori, slt, slti, sltiu, sltu, sub, \xor , xori;

  Comparator #(.width(6)) comparator_1 (.a(in_2), .b(6'b001000), .eq(addi));  // open: gt, lt
  Comparator #(.width(6)) comparator_2 (.a(in_2), .b(6'b001100), .eq(andi));  // open: gt, lt
  Comparator #(.width(6)) comparator_3 (.a(in_2), .b(6'b001101), .eq(ori));  // open: gt, lt
  Comparator #(.width(6)) comparator_4 (.a(in_2), .b(6'b001110), .eq(xori));  // open: gt, lt
  Comparator #(.width(6)) comparator_5 (.a(in_2), .b(6'b001010), .eq(slti));  // open: gt, lt
  Comparator #(.width(6)) comparator_6 (.a(in_2), .b(6'b001011), .eq(sltiu));  // open: gt, lt
  Comparator #(.width(6)) comparator_7 (.a(in_2), .b({6{1'b0}}), .eq(comparator_7_eq));  // open: gt, lt
  Comparator #(.width(6)) comparator_8 (.a(in_1), .b(6'b100000), .eq(comparator_8_eq));  // open: gt, lt
  Comparator #(.width(6)) comparator_9 (.a(in_1), .b(6'b100010), .eq(comparator_9_eq));  // open: gt, lt
  Comparator #(.width(6)) comparator_10 (.a(in_1), .b(6'b011000), .eq(comparator_10_eq));  // open: gt, lt
  Comparator #(.width(6)) comparator_11 (.a(in_1), .b(6'b011001), .eq(comparator_11_eq));  // open: gt, lt
  Comparator #(.width(6)) comparator_12 (.a(in_1), .b(6'b011010), .eq(comparator_12_eq));  // open: gt, lt
  Comparator #(.width(6)) comparator_13 (.a(in_1), .b(6'b011011), .eq(comparator_13_eq));  // open: gt, lt
  Comparator #(.width(6)) comparator_14 (.a(in_1), .b(6'b100100), .eq(comparator_14_eq));  // open: gt, lt
  Comparator #(.width(6)) comparator_15 (.a(in_1), .b(6'b100101), .eq(comparator_15_eq));  // open: gt, lt
  Comparator #(.width(6)) comparator_16 (.a(in_1), .b(6'b100111), .eq(comparator_16_eq));  // open: gt, lt
  Comparator #(.width(6)) comparator_17 (.a(in_1), .b(6'b101000), .eq(comparator_17_eq));  // open: gt, lt
  Comparator #(.width(6)) comparator_18 (.a(in_1), .b(6'b101010), .eq(comparator_18_eq));  // open: gt, lt
  Comparator #(.width(6)) comparator_19 (.a(in_1), .b(6'b101011), .eq(comparator_19_eq));  // open: gt, lt
  and and_1 (add, comparator_7_eq, comparator_8_eq);
  and and_2 (sub, comparator_7_eq, comparator_9_eq);
  and and_3 (mult, comparator_7_eq, comparator_10_eq);
  and and_4 (mulu, comparator_7_eq, comparator_11_eq);
  and and_5 (div, comparator_7_eq, comparator_12_eq);
  and and_6 (divu, comparator_7_eq, comparator_13_eq);
  and and_7 (\and , comparator_7_eq, comparator_14_eq);
  and and_8 (\or , comparator_7_eq, comparator_15_eq);
  and and_9 (\nor , comparator_7_eq, comparator_16_eq);
  and and_10 (\xor , comparator_7_eq, comparator_17_eq);
  and and_11 (slt, comparator_7_eq, comparator_18_eq);
  and and_12 (sltu, comparator_7_eq, comparator_19_eq);
  or or_1 (out_4, mult, div, slt, slti);
  or or_2 (L_HI_LO, mult, div, mulu, divu);
  or or_3 (Selector[0], sub, div, divu, \xor , \or , ori, xori);
  or or_4 (Selector[1], mult, mulu, div, \xor , divu, \nor , xori);
  or or_5 (Selector[2], \and , andi, \or , \xor , ori, \nor , xori);
  or or_6 (Selector[3], slt, sltu, slti, sltiu);
  and and_13 (and_13_out, in_3[15], ~andi, ~ori, ~xori);  // AND_Gate
  assign Output[31:15] = {{16{and_13_out}}, and_13_out};  // Bit_Extender bit_extender_1

  assign Output[14:0] = in_3[14:0];

  // Other names for the same wires on the sheet: Constante[15:0] = in_3; Func_Code[5:0] = in_1; Op_Code[5:0] = in_2
endmodule

module Divi (
  input  [31:0] in_1,
  input  [31:0] in_2,
  input  in_3,
  output [31:0] out_4,
  output [31:0] out_5
);

  wire SignA, SignB, SignResult;
  wire [31:0] A_t, adder_1_out, B_t, divider_1_out, multiplexer_4_out, negator_1_out, negator_2_out,
       negator_3_out, rem, subtractor_1_out;

  and and_1 (SignA, in_1[31], in_3);
  Multiplexer #(.width(32)) multiplexer_1 (.in0(in_1), .in1(negator_1_out), .out(A_t), .sel(SignA));  // open: en
  Negator #(.width(32)) negator_1 (.in(in_1), .out(negator_1_out));
  Multiplexer #(.width(32)) multiplexer_2 (.in0(in_2), .in1(negator_2_out), .out(B_t), .sel(SignB));  // open: en
  Negator #(.width(32)) negator_2 (.in(in_2), .out(negator_2_out));
  Divider #(.width(32)) divider_1 (.a(A_t), .b(B_t), .out(divider_1_out), .rem(rem));  // open: upper
  Subtractor #(.width(32)) subtractor_1 (.a(B_t), .b(rem), .out(subtractor_1_out));  // open: bin, bout
  Adder #(.width(32)) adder_1 (.a(divider_1_out), .b(32'h1), .out(adder_1_out));  // open: cin, cout
  Multiplexer #(.width(32)) multiplexer_3 (.in0(rem), .in1(subtractor_1_out), .out(out_5), .sel(SignA));  // open: en
  and and_2 (SignB, in_2[31], in_3);
  Multiplexer #(.width(32)) multiplexer_4 (
    .in0(divider_1_out), .in1(adder_1_out), .out(multiplexer_4_out), .sel(SignA));  // open: en
  Negator #(.width(32)) negator_3 (.in(multiplexer_4_out), .out(negator_3_out));
  xor xor_1 (SignResult, SignA, SignB);
  Multiplexer #(.width(32)) multiplexer_5 (
    .in0(multiplexer_4_out), .in1(negator_3_out), .out(out_4), .sel(SignResult));  // open: en

  // Other names for the same wires on the sheet: A[31:0] = in_1; B[31:0] = in_2; remainder[31:0] = out_5;
  //   Result[31:0] = out_4; Sign = in_3
endmodule

module Multi (
  input  [31:0] in_1,
  input  [31:0] in_2,
  input  in_3,
  output [31:0] HI,
  output [31:0] LO
);

  wire SignA, SignB;
  wire [31:0] Hi_t, Lo_t, multiplexer_1_out, multiplexer_2_out, negator_1_out, negator_2_out, UnSignedHi,
       UnSignedLo;

  and and_1 (SignA, in_1[31], in_3);
  Negator #(.width(32)) negator_1 (.in(in_1), .out(negator_1_out));
  Negator #(.width(32)) negator_2 (.in(in_2), .out(negator_2_out));
  Multiplier #(.width(32)) multiplier_1 (.a(in_1), .b(in_2), .out(Lo_t), .cout(Hi_t));  // open: cin
  Multiplexer #(.width(32)) multiplexer_1 (
    .in0(in_1), .in1(negator_1_out), .out(multiplexer_1_out), .sel(SignA));  // open: en
  Multiplexer #(.width(32)) multiplexer_2 (
    .in0(in_2), .in1(negator_2_out), .out(multiplexer_2_out), .sel(SignB));  // open: en
  and and_2 (SignB, in_2[31], in_3);
  Multiplier #(.width(32)) multiplier_2 (
    .a(multiplexer_1_out), .b(multiplexer_2_out), .out(UnSignedLo), .cout(UnSignedHi));  // open: cin
  Multiplexer #(.width(32)) multiplexer_3 (.in0(UnSignedHi), .in1(Hi_t), .out(HI), .sel(in_3));  // open: en
  Multiplexer #(.width(32)) multiplexer_4 (.in0(UnSignedLo), .in1(Lo_t), .out(LO), .sel(in_3));  // open: en

  // Other names for the same wires on the sheet: A[31:0] = in_1; B[31:0] = in_2; Sign = in_3
endmodule

module Comparer (
  input  [31:0] in_1,
  input  [31:0] in_2,
  input  in_3,
  output [31:0] Output
);

  wire multiplexer_1_out, slt, sltu;

  Comparator #(.width(32)) comparator_1 (.a(in_1), .b(in_2), .lt(slt));  // open: gt, eq
  Comparator #(.width(32), .mode("unsigned")) comparator_2 (.a(in_1), .b(in_2), .lt(sltu));  // open: gt, eq
  Multiplexer multiplexer_1 (.in0(sltu), .in1(slt), .out(multiplexer_1_out), .sel(in_3));  // open: en
  assign Output = {{31{1'b0}}, multiplexer_1_out};  // Bit_Extender bit_extender_1

  // Other names for the same wires on the sheet: A[31:0] = in_1; B[31:0] = in_2; Out[31:0] = Output; Sign = in_3
endmodule
