// Logisim project Control.circ as structural Verilog
module Control_Unit (
  input  in_1,
  input  in_2,
  input  in_3,
  input  in_4,
  input  in_5,
  input  in_6,
  input  [5:0] in_7,
  input  [5:0] in_8,
  output Get_Inst,
  output PCen,
  output SPen,
  output INSTen,
  output KBDen,
  output RegW,
  output TTYen,
  output WriteD,
  output startEN,
  output Get_Data,
  output End
);

  wire ALU, and_1_out, and_2_out, and_3_out, and_5_out, Copy, d_ff_1_q, d_ff_5_q, d_ff_6_q, d_ff_8_q,
       d_ff_9_q, demultiplexer_1_out0, demultiplexer_2_out0, demultiplexer_3_out0, demultiplexer_4_out0,
       demultiplexer_4_out1, halt, Jump, kbd, lw, Memory, or_1_out, or_2_out, or_3_out, or_5_out, pop, push,
       \rand , SP_1, SP_2, Specials, startEN_t, sw, tty;

  D_Flip_Flop #(.trigger("falling")) d_ff_1 (
    .clk(in_2), .D(Memory), .Q(d_ff_1_q), .reset(in_3));  // open: Qn, preset, en
  or or_1 (or_1_out, End, and_1_out);
  and and_1 (and_1_out, Specials, halt);
  and and_2 (and_2_out, Specials, \rand );
  and and_3 (and_3_out, Specials, kbd);
  Demultiplexer #(.enable("false")) demultiplexer_1 (
    .out0(demultiplexer_1_out0), .out1(Get_Data), .in(d_ff_1_q), .sel(or_2_out));
  or or_2 (or_2_out, lw, pop);
  D_Flip_Flop #(.trigger("falling")) d_ff_2 (.clk(in_2), .D(or_1_out), .Q(End), .reset(in_3));  // open: Qn, preset, en
  Demultiplexer #(.enable("false")) demultiplexer_2 (
    .out0(demultiplexer_2_out0), .out1(SP_1), .in(demultiplexer_1_out0), .sel(push));
  or or_3 (or_3_out, ALU, Copy, and_2_out, and_3_out, in_5);
  Operations operations_1 (
    .in_1(in_8), .in_2(in_7), .EN(startEN_t), .ALU(ALU), .Copy(Copy), .Jump(Jump), .Memory(Memory),
    .Specials(Specials));
  D_Flip_Flop #(.trigger("falling")) d_ff_3 (.clk(in_2), .D(or_3_out), .Q(RegW));  // open: Qn, preset, en, reset
  D_Flip_Flop #(.trigger("falling")) d_ff_4 (
    .clk(in_2), .D(in_4), .Q(startEN_t), .reset(in_3));  // open: Qn, preset, en
  D_Flip_Flop #(.trigger("falling")) d_ff_5 (.clk(in_2), .D(RegW), .Q(d_ff_5_q), .reset(in_3));  // open: Qn, preset, en
  D_Flip_Flop #(.trigger("falling")) d_ff_6 (.clk(in_2), .D(SP_1), .Q(d_ff_6_q), .reset(in_3));  // open: Qn, preset, en
  Demultiplexer #(.enable("false")) demultiplexer_3 (
    .out0(demultiplexer_3_out0), .out1(SP_2), .in(d_ff_5_q), .sel(pop));
  D_Flip_Flop #(.trigger("falling")) d_ff_7 (
    .clk(in_2), .Q(startEN), .preset(startEN_t), .reset(PCen));  // open: D, Qn, en
  or or_4 (WriteD, demultiplexer_2_out0, d_ff_6_q);
  and and_4 (KBDen, kbd, demultiplexer_3_out0);
  D_Flip_Flop #(.trigger("falling")) d_ff_8 (.clk(in_2), .D(SP_2), .Q(d_ff_8_q), .reset(in_3));  // open: Qn, preset, en
  Other_OP_Decoder other_op_decoder_1 (
    .OP_Code(in_7), .Func_Code(in_8), .Start(1'b1), .pop(pop), .push(push), .lw(lw), .sw(sw), .tty(tty),
    .rnd(\rand ), .kbd(kbd), .halt(halt));  // open: mfhi, mflo
  D_Flip_Flop #(.trigger("falling")) d_ff_9 (
    .clk(in_2), .D(demultiplexer_4_out0), .Q(d_ff_9_q), .preset(in_3));  // open: Qn, en, reset
  and and_5 (and_5_out, Specials, tty);
  Demultiplexer #(.enable("false")) demultiplexer_4 (
    .out0(demultiplexer_4_out0), .out1(demultiplexer_4_out1), .in(d_ff_9_q), .sel(in_1));
  or or_5 (or_5_out, demultiplexer_3_out0, in_6, Jump, and_5_out, d_ff_8_q);
  or or_6 (Get_Inst, demultiplexer_4_out1, PCen);
  D_Flip_Flop #(.trigger("falling")) IDLE (.clk(in_2), .D(or_5_out), .Q(PCen), .reset(in_3));  // open: Qn, preset, en
  or or_7 (SPen, SP_1, SP_2);
  and and_6 (TTYen, Specials, tty, startEN);

  assign INSTen = in_4;

  // Other names for the same wires on the sheet: CLK = in_2; En = startEN; F_Code[5:0] = in_8; kbd_EN = KBDen;
  //   Op_code[5:0] = in_7; Ready_Data = in_5; Inst_EN = in_4; Ready_Inst = in_4; Ready_Write = in_6; RegEN = RegW;
  //   Res = in_3; START = in_1; stopEN = PCen; Write_Data = WriteD
endmodule

module Operations (
  input  [5:0] in_1,
  input  [5:0] in_2,
  input  EN,
  output ALU,
  output Copy,
  output Jump,
  output Memory,
  output Specials
);

  wire ALU_t, and_1_out, and_2_out, and_3_out, and_4_out, and_5_out, comparator_1_eq, comparator_2_eq,
       comparator_3_eq, comparator_4_eq, comparator_5_eq, comparator_6_eq, comparator_7_lt, comparator_8_eq,
       comparator_9_eq, comparator_10_eq, Copy_t, I, J, Jump_t, Memory_t, R, Specials_t;

  OP_Identifirer op_identifirer_1 (.OP_Code(in_2), .J(J), .R(R), .I(I));
  Comparator #(.width(6), .mode("unsigned")) comparator_1 (
    .a(in_2), .b({6{1'b0}}), .eq(comparator_1_eq));  // open: gt, lt
  Comparator #(.width(6), .mode("unsigned")) comparator_2 (
    .a(in_1), .b(6'b010010), .eq(comparator_2_eq));  // open: gt, lt
  Comparator #(.width(6), .mode("unsigned")) comparator_3 (
    .a(in_1), .b(6'b010000), .eq(comparator_3_eq));  // open: gt, lt
  Comparator #(.width(6), .mode("unsigned")) comparator_4 (
    .a(in_2), .b({6{1'b0}}), .eq(comparator_4_eq));  // open: gt, lt
  Comparator #(.width(6), .mode("unsigned")) comparator_5 (
    .a(in_1), .b({6{1'b0}}), .eq(comparator_5_eq));  // open: gt, lt
  Comparator #(.width(6), .mode("unsigned")) comparator_6 (
    .a(in_1), .b(6'b001000), .eq(comparator_6_eq));  // open: gt, lt
  Comparator #(.width(6), .mode("unsigned")) comparator_7 (
    .a(in_2), .b(6'b001000), .lt(comparator_7_lt));  // open: gt, eq
  Comparator #(.width(6), .mode("unsigned")) comparator_8 (
    .a(in_2), .b(6'b111000), .eq(comparator_8_eq));  // open: gt, lt
  Comparator #(.width(6), .mode("unsigned")) comparator_9 (
    .a(in_2), .b(6'b100011), .eq(comparator_9_eq));  // open: gt, lt
  Comparator #(.width(6), .mode("unsigned")) comparator_10 (
    .a(in_2), .b(6'b101011), .eq(comparator_10_eq));  // open: gt, lt
  Comparator #(.width(6), .mode("unsigned")) comparator_11 (.a(in_2), .b({6{1'b1}}), .eq(Specials_t));  // open: gt, lt
  and and_1 (and_1_out, comparator_1_eq, comparator_2_eq);
  and and_2 (and_2_out, comparator_1_eq, comparator_3_eq);
  and and_3 (and_3_out, comparator_4_eq, comparator_5_eq);
  and and_4 (and_4_out, comparator_4_eq, comparator_6_eq);
  and and_5 (and_5_out, I, comparator_7_lt);
  nor nor_1 (ALU_t, Copy_t, Jump_t, Memory_t, Specials_t);
  or or_1 (Copy_t, and_1_out, and_2_out);
  or or_2 (Jump_t, and_3_out, and_4_out, and_5_out);
  or or_3 (Memory_t, comparator_8_eq, comparator_9_eq, comparator_10_eq);
  and and_6 (ALU, EN, ALU_t);
  and and_7 (Copy, EN, Copy_t);
  and and_8 (Jump, EN, Jump_t);
  and and_9 (Memory, EN, Memory_t);
  and and_10 (Specials, EN, Specials_t);

  // Other names for the same wires on the sheet: Func_Code[5:0] = in_1; Op_Code[5:0] = in_2
endmodule

module OP_Identifirer (
  input  [5:0] OP_Code,
  output J,
  output R,
  output I
);

  wire comparator_2_eq, comparator_3_eq, comparator_4_eq;

  Comparator #(.width(6)) comparator_1 (.a(OP_Code), .b(6'b000010), .eq(J));  // open: gt, lt
  Comparator #(.width(6)) comparator_2 (.a(OP_Code), .b({6{1'b0}}), .eq(comparator_2_eq));  // open: gt, lt
  Comparator #(.width(6)) comparator_3 (.a(OP_Code), .b({6{1'b1}}), .eq(comparator_3_eq));  // open: gt, lt
  Comparator #(.width(6)) comparator_4 (.a(OP_Code), .b(6'b111000), .eq(comparator_4_eq));  // open: gt, lt
  or or_1 (R, comparator_2_eq, comparator_3_eq, comparator_4_eq);
  and and_1 (I, R, J);
endmodule

module Other_OP_Decoder (
  input  [5:0] OP_Code,
  input  [5:0] Func_Code,
  input  Start,
  output mfhi,
  output mflo,
  output pop,
  output push,
  output lw,
  output sw,
  output tty,
  output rnd,
  output kbd,
  output halt
);

  wire and_1_out, and_2_out, and_3_out, and_4_out, and_5_out, and_6_out, and_7_out, and_8_out,
       comparator_1_eq, comparator_2_eq, comparator_3_eq, comparator_4_eq, comparator_5_eq, comparator_6_eq,
       comparator_7_eq, comparator_8_eq, comparator_9_eq, comparator_10_eq, comparator_11_eq,
       comparator_12_eq, comparator_13_eq;

  Comparator #(.width(6)) comparator_1 (.a(OP_Code), .b({6{1'b0}}), .eq(comparator_1_eq));  // open: gt, lt
  Comparator #(.width(6)) comparator_2 (.a(Func_Code), .b(6'b010000), .eq(comparator_2_eq));  // open: gt, lt
  Comparator #(.width(6)) comparator_3 (.a(Func_Code), .b(6'b010010), .eq(comparator_3_eq));  // open: gt, lt
  Comparator #(.width(6)) comparator_4 (.a(OP_Code), .b(6'b111000), .eq(comparator_4_eq));  // open: gt, lt
  Comparator #(.width(6)) comparator_5 (.a(Func_Code), .b({6{1'b0}}), .eq(comparator_5_eq));  // open: gt, lt
  Comparator #(.width(6)) comparator_6 (.a(Func_Code), .b(6'b000001), .eq(comparator_6_eq));  // open: gt, lt
  Comparator #(.width(6)) comparator_7 (.a(OP_Code), .b(6'b100011), .eq(comparator_7_eq));  // open: gt, lt
  Comparator #(.width(6)) comparator_8 (.a(OP_Code), .b(6'b101011), .eq(comparator_8_eq));  // open: gt, lt
  Comparator #(.width(6)) comparator_9 (.a(OP_Code), .b({6{1'b1}}), .eq(comparator_9_eq));  // open: gt, lt
  Comparator #(.width(6)) comparator_10 (.a(Func_Code), .b(6'b000001), .eq(comparator_10_eq));  // open: gt, lt
  Comparator #(.width(6)) comparator_11 (.a(Func_Code), .b(6'b000010), .eq(comparator_11_eq));  // open: gt, lt
  Comparator #(.width(6)) comparator_12 (.a(Func_Code), .b(6'b000100), .eq(comparator_12_eq));  // open: gt, lt
  Comparator #(.width(6)) comparator_13 (.a(Func_Code), .b({6{1'b1}}), .eq(comparator_13_eq));  // open: gt, lt
  and and_1 (and_1_out, comparator_1_eq, comparator_2_eq);
  and and_2 (and_2_out, comparator_1_eq, comparator_3_eq);
  and and_3 (and_3_out, comparator_4_eq, comparator_5_eq);
  and and_4 (and_4_out, comparator_4_eq, comparator_6_eq);
  and and_5 (and_5_out, comparator_9_eq, comparator_10_eq);
  and and_6 (and_6_out, comparator_9_eq, comparator_11_eq);
  and and_7 (and_7_out, comparator_9_eq, comparator_12_eq);
  and and_8 (and_8_out, comparator_9_eq, comparator_13_eq);
  and and_9 (mfhi, Start, and_1_out);
  and and_10 (mflo, Start, and_2_out);
  and and_11 (pop, Start, and_3_out);
  and and_12 (push, Start, and_4_out);
  and and_13 (lw, Start, comparator_7_eq);
  and and_14 (sw, Start, comparator_8_eq);
  and and_15 (tty, Start, and_5_out);
  and and_16 (rnd, Start, and_6_out);
  and and_17 (kbd, Start, and_7_out);
  and and_18 (halt, Start, and_8_out);
endmodule
