// Logisim project RAM.circ as structural Verilog
module Delay (
  input  [3:0] in_1,
  input  in_2,
  input  in_3,
  input  in_4,
  output Ready
);

  wire [3:0] counter_1_q;

  Counter #(.width(4), .max('hf)) counter_1 (
    .count(in_2), .Q(counter_1_q), .clk(in_3), .clr(in_4));  // open: load, D, carry
  Comparator #(.width(4)) comparator_1 (.a(counter_1_q), .b(in_1), .eq(Ready));  // open: gt, lt

  // Other names for the same wires on the sheet: CLK = in_3; RES = in_4; Start = in_2; Time[3:0] = in_1
endmodule

module Reading (
  input  [3:0] in_1,
  input  [31:0] in_2,
  input  [31:0] in_3,
  input  [31:0] in_4,
  input  [31:0] in_5,
  input  in_6,
  input  in_7,
  input  in_8,
  output CS,
  output [31:0] Ram_00,
  output Ready,
  output [31:0] Ram_01,
  output [31:0] Ram_10,
  output [31:0] Ram_11
);

  wire delay_1_ready, EN, or_1_out, Start;
  wire [31:0] _00, _01, _10, _11;

  or or_1 (or_1_out, in_6, delay_1_ready);
  D_Flip_Flop #(.trigger("falling")) d_ff_1 (
    .clk(in_7), .D(in_6), .Q(Start), .en(or_1_out));  // open: Qn, preset, reset
  Register #(.width(32)) register_1 (.D(_00), .en(EN), .Q(Ram_00), .clk(in_7), .clr(in_8));
  Register #(.width(32)) register_2 (.D(_01), .en(EN), .Q(Ram_01), .clk(in_7), .clr(in_8));
  Register #(.width(32)) register_3 (.D(_10), .en(EN), .Q(Ram_10), .clk(in_7), .clr(in_8));
  Register #(.width(32)) register_4 (.D(_11), .en(EN), .Q(Ram_11), .clk(in_7), .clr(in_8));
  Delay delay_1 (.in_1(in_1), .in_2(Start), .in_3(in_7), .in_4(Ready), .Ready(delay_1_ready));
  D_Flip_Flop #(.trigger("falling")) d_ff_2 (
    .clk(in_7), .D(delay_1_ready), .Q(EN), .reset(Ready));  // open: Qn, preset, en
  or or_2 (CS, Start, EN);
  D_Flip_Flop #(.trigger("falling")) d_ff_3 (.clk(in_7), .D(EN), .Q(Ready));  // open: Qn, preset, en, reset

  // Other names for the same wires on the sheet: CLK = in_7; Ram_00_t[31:0] = in_2; Ram_01_t[31:0] = in_3;
  //   Ram_10_t[31:0] = in_4; Ram_11_t[31:0] = in_5; Read = in_6; RES = in_8; Time[3:0] = in_1
endmodule

module Access (
  input  [31:0] in_1,
  input  [31:0] in_2,
  input  [31:0] in_3,
  input  [31:0] in_4,
  input  [31:0] in_5,
  input  [3:0] in_6,
  input  [3:0] in_7,
  input  in_8,
  input  in_9,
  input  in_10,
  input  in_11,
  input  in_12,
  input  in_13,
  output [3:0] Mask,
  output [31:0] RAM_OUT,
  output RW,
  output Chip_Select,
  output Ready_Inst,
  output [15:0] Address,
  output Ready_Data,
  output Ready_write
);

  wire CS_Data, CS_Inst, delay_1_ready, EN, or_1_out;
  wire [31:0] _00_Out, _01_Out, _10_Out, _11_Out, D0_Out, D1_Out, D2_Out, D3_Out, I0_Out, I1_Out, I2_Out,
       I3_Out;

  D_Flip_Flop #(.trigger("falling")) d_ff_1 (.clk(in_9), .D(in_8), .Q(RW), .en(or_1_out));  // open: Qn, preset, reset
  or or_1 (or_1_out, in_8, delay_1_ready);
  Multiplexer #(.width(32), .enable("false")) multiplexer_1 (.in0(D0_Out), .in1(I0_Out), .out(_00_Out), .sel(in_13));
  or or_2 (Chip_Select, RW, CS_Inst, CS_Data);
  Multiplexer #(.width(32), .enable("false")) multiplexer_2 (.in0(D1_Out), .in1(I1_Out), .out(_01_Out), .sel(in_13));
  Delay delay_1 (.in_1(in_7), .in_2(RW), .in_3(in_9), .in_4(Ready_write), .Ready(delay_1_ready));
  Reading reading_1 (
    .in_1(in_6), .in_2(in_2), .in_3(in_3), .in_4(in_4), .in_5(in_5), .in_6(in_11), .in_7(in_9), .in_8(in_10),
    .CS(CS_Inst), .Ram_00(I0_Out), .Ready(Ready_Inst), .Ram_01(I1_Out), .Ram_10(I2_Out), .Ram_11(I3_Out));
  Reading reading_2 (
    .in_1(in_6), .in_2(in_2), .in_3(in_3), .in_4(in_4), .in_5(in_5), .in_6(in_12), .in_7(in_9), .in_8(in_10),
    .CS(CS_Data), .Ram_00(D0_Out), .Ready(Ready_Data), .Ram_01(D1_Out), .Ram_10(D2_Out), .Ram_11(D3_Out));
  D_Flip_Flop #(.trigger("falling")) d_ff_2 (
    .clk(in_9), .D(delay_1_ready), .Q(EN), .reset(Ready_write));  // open: Qn, preset, en
  Multiplexer #(.width(32), .enable("false")) multiplexer_3 (.in0(D2_Out), .in1(I2_Out), .out(_10_Out), .sel(in_13));
  D_Flip_Flop #(.trigger("falling")) d_ff_3 (.clk(in_9), .D(EN), .Q(Ready_write));  // open: Qn, preset, en, reset
  Decoder #(.select(2), .enable("false")) decoder_1 (
    .out0(Mask[0]), .out1(Mask[1]), .out2(Mask[2]), .out3(Mask[3]), .sel(in_1[3:2]));
  Multiplexer #(.width(32), .enable("false")) multiplexer_4 (.in0(D3_Out), .in1(I3_Out), .out(_11_Out), .sel(in_13));
  Multiplexer #(.select(2), .width(32), .enable("false")) multiplexer_5 (
    .in0(_00_Out), .in1(_01_Out), .in2(_10_Out), .in3(_11_Out),
    .out({RAM_OUT[7:0], RAM_OUT[15:8], RAM_OUT[23:16], RAM_OUT[31:24]}), .sel(in_1[3:2]));

  assign Address = in_1[19:4];

  // Other names for the same wires on the sheet: _00[31:0] = in_2; _01[31:0] = in_3; _10[31:0] = in_4;
  //   _11[31:0] = in_5; CLK = in_9; DP_Address[31:0] = in_1; Mask_t[1:0] = in_1[3:2]; Adress[15:0] = in_1[19:4];
  //   Load = in_13; Read_Data = in_12; Read_Inst = in_11; Read_Time[3:0] = in_6; Ready_W = Ready_write; RES = in_10;
  //   RW_t = in_8; Start = RW; Write_Time[3:0] = in_7
endmodule
