// Logisim project datha pad File.circ as structural Verilog
module File (
  input  [31:0] in_1,
  input  [31:0] in_2,
  input  [31:0] in_3,
  input  [4:0] in_4,
  input  [4:0] in_5,
  input  [4:0] in_6,
  input  in_7,
  input  in_8,
  input  in_9,
  input  in_10,
  input  in_11,
  input  in_12,
  input  in_13,
  input  in_14,
  input  in_15,
  input  in_16,
  output [31:0] out_17,
  output [31:0] out_18,
  output [31:0] Output,
  output [31:0] out_20,
  output [31:0] out_21
);

  wire and_1_out, L0, L1, L2, L3, L4, L5, L6, L7, L8, L9, L10, L11, L12, L13, L14, L15, L16, L17, L18, L19,
       L20, L21, L22, L23, L24, L25, L26, L27, L28, L29, L30, L31, LSP, or_1_out;
  wire [1:0] Selector;
  wire [31:0] adder_1_out, Input, multiplexer_2_out, multiplexer_6_out, Q0, Q1, Q2, Q3, Q4, Q5, Q6, Q7, Q8,
       Q9, Q10, Q11, Q12, Q13, Q14, Q15, Q16, Q17, Q18, Q19, Q20, Q21, Q22, Q23, Q24, Q25, Q26, Q27, Q28,
       Q29, Q30, Random, SP;

  Register #(.width(32)) register_1 (.D({32{1'b0}}), .en(L0), .Q(Q0), .clk(in_11), .clr(in_9));
  Register #(.width(32)) register_2 (.D(Input), .en(L8), .Q(Q8), .clk(in_11), .clr(in_9));
  Register #(.width(32)) register_3 (.D(Input), .en(L16), .Q(Q16), .clk(in_11), .clr(in_9));
  Register #(.width(32)) register_4 (.D(Input), .en(L24), .Q(Q24), .clk(in_11), .clr(in_9));
  Register #(.width(32)) register_5 (.D(in_2), .en(in_13), .Q(out_17), .clk(in_11), .clr(in_9));
  or or_1 (or_1_out, in_15, in_16);
  and and_1 (and_1_out, or_1_out, in_8);
  Multiplexer #(.select(2), .width(32), .enable("false")) multiplexer_1 (
    .in0(in_1), .in1(out_17), .in2(out_21), .in3(Random), .out(Input), .sel(Selector));
  or or_2 (Selector[0], in_10, in_12);
  or or_3 (Selector[1], in_14, in_10);
  Multiplexer #(.width(32), .enable("false")) multiplexer_2 (
    .in0(32'h4), .in1(32'hfffffffc), .out(multiplexer_2_out), .sel(in_15));
  Random #(.width(32), .seed(7)) random_1 (.clk(in_11), .out(Random));  // open: next, clr
  Register #(.width(32)) register_6 (.D(Input), .en(L1), .Q(Q1), .clk(in_11), .clr(in_9));
  Register #(.width(32)) register_7 (.D(Input), .en(L9), .Q(Q9), .clk(in_11), .clr(in_9));
  Register #(.width(32)) register_8 (.D(Input), .en(L17), .Q(Q17), .clk(in_11), .clr(in_9));
  Register #(.width(32)) register_9 (.D(Input), .en(L25), .Q(Q25), .clk(in_11), .clr(in_9));
  Adder #(.width(32)) adder_1 (.a(multiplexer_2_out), .b(out_18), .out(adder_1_out));  // open: cin, cout
  Register #(.width(32)) register_10 (.D(in_3), .en(in_13), .Q(out_21), .clk(in_11), .clr(in_9));
  or or_4 (LSP, and_1_out, L31, in_9);
  Multiplexer #(.width(32), .enable("false")) multiplexer_3 (.in0(adder_1_out), .out(SP), .sel(in_9));  // open: in1
  Register #(.width(32)) register_11 (.D(Input), .en(L2), .Q(Q2), .clk(in_11), .clr(in_9));
  Register #(.width(32)) register_12 (.D(Input), .en(L10), .Q(Q10), .clk(in_11), .clr(in_9));
  Register #(.width(32)) register_13 (.D(Input), .en(L18), .Q(Q18), .clk(in_11), .clr(in_9));
  Register #(.width(32)) register_14 (.D(Input), .en(L26), .Q(Q26), .clk(in_11), .clr(in_9));
  Demultiplexer #(.select(5)) demultiplexer_1 (
    .out0(L0), .out1(L1), .out2(L2), .out3(L3), .out4(L4), .out5(L5), .out6(L6), .out7(L7), .out8(L8),
    .out9(L9), .out10(L10), .out11(L11), .out12(L12), .out13(L13), .out14(L14), .out15(L15), .out16(L16),
    .out17(L17), .out18(L18), .out19(L19), .out20(L20), .out21(L21), .out22(L22), .out23(L23), .out24(L24),
    .out25(L25), .out26(L26), .out27(L27), .out28(L28), .out29(L29), .out30(L30), .out31(L31), .in(in_7),
    .sel(in_4));  // open: en
  Register #(.width(32)) register_15 (.D(Input), .en(L3), .Q(Q3), .clk(in_11), .clr(in_9));
  Register #(.width(32)) register_16 (.D(Input), .en(L11), .Q(Q11), .clk(in_11), .clr(in_9));
  Register #(.width(32)) register_17 (.D(Input), .en(L19), .Q(Q19), .clk(in_11), .clr(in_9));
  Register #(.width(32)) register_18 (.D(Input), .en(L27), .Q(Q27), .clk(in_11), .clr(in_9));
  Register #(.width(32)) register_19 (.D(Input), .en(L4), .Q(Q4), .clk(in_11), .clr(in_9));
  Register #(.width(32)) register_20 (.D(Input), .en(L12), .Q(Q12), .clk(in_11), .clr(in_9));
  Register #(.width(32)) register_21 (.D(Input), .en(L20), .Q(Q20), .clk(in_11), .clr(in_9));
  Register #(.width(32)) register_22 (.D(Input), .en(L28), .Q(Q28), .clk(in_11), .clr(in_9));
  Multiplexer #(.select(5), .width(32)) multiplexer_4 (
    .in0(Q0), .in1(Q1), .in2(Q2), .in3(Q3), .in4(Q4), .in5(Q5), .in6(Q6), .in7(Q7), .in8(Q8), .in9(Q9),
    .in10(Q10), .in11(Q11), .in12(Q12), .in13(Q13), .in14(Q14), .in15(Q15), .in16(Q16), .in17(Q17),
    .in18(Q18), .in19(Q19), .in20(Q20), .in21(Q21), .in22(Q22), .in23(Q23), .in24(Q24), .in25(Q25),
    .in26(Q26), .in27(Q27), .in28(Q28), .in29(Q29), .in30(Q30), .in31(out_18), .out(Output), .sel(in_5));  // open: en
  Register #(.width(32)) register_23 (.D(Input), .en(L5), .Q(Q5), .clk(in_11), .clr(in_9));
  Register #(.width(32)) register_24 (.D(Input), .en(L13), .Q(Q13), .clk(in_11), .clr(in_9));
  Register #(.width(32)) register_25 (.D(Input), .en(L21), .Q(Q21), .clk(in_11), .clr(in_9));
  Register #(.width(32)) register_26 (.D(Input), .en(L29), .Q(Q29), .clk(in_11), .clr(in_9));
  Multiplexer #(.select(5), .width(32)) multiplexer_5 (
    .in0(Q0), .in1(Q1), .in2(Q2), .in3(Q3), .in4(Q4), .in5(Q5), .in6(Q6), .in7(Q7), .in8(Q8), .in9(Q9),
    .in10(Q10), .in11(Q11), .in12(Q12), .in13(Q13), .in14(Q14), .in15(Q15), .in16(Q16), .in17(Q17),
    .in18(Q18), .in19(Q19), .in20(Q20), .in21(Q21), .in22(Q22), .in23(Q23), .in24(Q24), .in25(Q25),
    .in26(Q26), .in27(Q27), .in28(Q28), .in29(Q29), .in30(Q30), .in31(out_18), .out(out_20), .sel(in_6));  // open: en
  Register #(.width(32)) register_27 (.D(Input), .en(L6), .Q(Q6), .clk(in_11), .clr(in_9));
  Register #(.width(32)) register_28 (.D(Input), .en(L14), .Q(Q14), .clk(in_11), .clr(in_9));
  Register #(.width(32)) register_29 (.D(Input), .en(L22), .Q(Q22), .clk(in_11), .clr(in_9));
  Register #(.width(32)) register_30 (.D(Input), .en(L30), .Q(Q30), .clk(in_11), .clr(in_9));
  Register #(.width(32)) register_31 (.D(Input), .en(L7), .Q(Q7), .clk(in_11), .clr(in_9));
  Register #(.width(32)) register_32 (.D(Input), .en(L15), .Q(Q15), .clk(in_11), .clr(in_9));
  Register #(.width(32)) register_33 (.D(Input), .en(L23), .Q(Q23), .clk(in_11), .clr(in_9));
  Multiplexer #(.width(32), .enable("false")) multiplexer_6 (.in0(SP), .in1(Input), .out(multiplexer_6_out), .sel(L31));
  Register #(.width(32)) register_34 (.D(multiplexer_6_out), .en(LSP), .Q(out_18), .clk(in_11), .clr(in_9));

  // Other names for the same wires on the sheet: A[31:0] = Output; Address[4:0] = in_4; B[31:0] = out_20; CLK = in_11;
  //   DHI[31:0] = in_2; DI[31:0] = in_1; DLO[31:0] = in_3; L_HI_LO = in_13; mfhi = in_12; mflo = in_14; Pop = in_16;
  //   Push = in_15; Q31[31:0] = out_18; QHI[31:0] = out_17; QLO[31:0] = out_21; random_t = in_10; Reset = in_9;
  //   RW = in_7; Sa[4:0] = in_5; Sb[4:0] = in_6; SPEN = in_8
endmodule
