// Logisim project s-mips.circ as structural Verilog
module S_MIPS_Board (
  input  DESHABILITAR_DISPATCHER,
  output halt
);

  wire button_1_out, CLK, CS, d_ff_1_q, LCLR, LoadRAM, LoadRAMOn, LW, R_R_W, R_W, ram_dispatcher_1_finished,
       RCS, Reset_out, RST, TTY_EN;
  wire [2:0] KDB;
  wire [3:0] LMask, Mask, ram_1_read_time, ram_1_write_time, RMask;
  wire [6:0] KDB_DATA, TTY_DATA;
  wire [15:0] Addr, LAddr, RAddr;
  wire [31:0] I0, I1, I2, I3, LData, ram_1_data_out_0, ram_1_data_out_1, ram_1_data_out_2, ram_1_data_out_3,
       RI0, RI1, RI2, RI3;

  TTY #(.rows(25), .cols(80)) tty_1 (.data(TTY_DATA), .clk(CLK), .we(TTY_EN), .clr(RST));
  not not_1 (LoadRAMOn, ram_dispatcher_1_finished);
  RAM_Dispatcher ram_dispatcher_1 (
    .WriteTime(ram_1_write_time), .Clock(CLK), .Data(LData), .Address(LAddr), .Mask(LMask),
    .Finished(ram_dispatcher_1_finished), .Write(LW), .CLR(LCLR));
  Keyboard #(.buflen(64)) keyboard_1 (.clk(CLK), .re(KDB[0]), .avail(KDB[2]), .data(KDB_DATA));  // open: clr
  RAM ram_1 (
    .Address(RAddr), .Data_Out_0(ram_1_data_out_0), .Data_Out_1(ram_1_data_out_1),
    .Data_Out_2(ram_1_data_out_2), .Data_Out_3(ram_1_data_out_3), .Data_In_0(RI0), .Data_In_1(RI1),
    .Data_In_2(RI2), .Data_In_3(RI3), .Mask(RMask), .nRead_Write(R_R_W), .Chip_Select(RCS),
    .Read_Time(ram_1_read_time), .Reset(button_1_out), .Write_Time(ram_1_write_time));
  Button button_1 (.out(button_1_out));
  D_Flip_Flop d_ff_1 (.clk(CLK), .D(1'b1), .Q(d_ff_1_q), .reset(Reset_out));  // open: Qn, preset, en
  Button Reset (.out(Reset_out));
  S_MIPS s_mips_1 (
    .Kbd_Enable(KDB[0]), .Address(Addr), .Kbd_Clear(KDB[1]), .Kbd_Available(KDB[2]), .RAM_In_0(I0),
    .Kbd_ASCII_Data(KDB_DATA), .RAM_In_1(I1), .TTY_Enable(TTY_EN), .RAM_In_2(I2), .RAM_In_3(I3),
    .TTY_ASCII_Data(TTY_DATA), .Reset(RST), .RAM_Out_0(ram_1_data_out_0), .Clock(CLK),
    .RAM_Out_1(ram_1_data_out_1), .Stop(halt), .RAM_Out_2(ram_1_data_out_2), .RAM_Out_3(ram_1_data_out_3),
    .Mask(Mask), .Read_Time(ram_1_read_time), .Write_Time(ram_1_write_time), .nRead_Write(R_W),
    .Chip_Select(CS));
  D_Flip_Flop d_ff_2 (.clk(CLK), .D(d_ff_1_q), .Qn(LCLR), .reset(Reset_out));  // open: Q, preset, en
  or or_1 (RST, LCLR, LoadRAM);
  Clock clock_1 (.out(CLK));
  Multiplexer #(.width(32), .enable("false")) multiplexer_1 (.in0(I0), .in1(LData), .out(RI0), .sel(LoadRAM));
  Multiplexer #(.width(32), .enable("false")) multiplexer_2 (.in0(I1), .in1(LData), .out(RI1), .sel(LoadRAM));
  Multiplexer #(.width(32), .enable("false")) multiplexer_3 (.in0(I2), .in1(LData), .out(RI2), .sel(LoadRAM));
  Multiplexer #(.width(32), .enable("false")) multiplexer_4 (.in0(I3), .in1(LData), .out(RI3), .sel(LoadRAM));
  and and_1 (LoadRAM, ~DESHABILITAR_DISPATCHER, LoadRAMOn);  // AND_Gate
  Multiplexer #(.width(16), .enable("false")) multiplexer_5 (.in0(Addr), .in1(LAddr), .out(RAddr), .sel(LoadRAM));
  Multiplexer #(.width(4), .enable("false")) multiplexer_6 (.in0(Mask), .in1(LMask), .out(RMask), .sel(LoadRAM));
  Multiplexer #(.enable("false")) multiplexer_7 (.in0(CS), .in1(LW), .out(RCS), .sel(LoadRAM));
  Multiplexer #(.enable("false")) multiplexer_8 (.in0(R_W), .in1(LW), .out(R_R_W), .sel(LoadRAM));

  // Notes on the sheet:
  //   NO MODIFICAR
  //   Keyboard
endmodule

module RAM (
  input  [15:0] Address,
  input  [31:0] Data_In_0,
  input  [31:0] Data_In_1,
  input  [31:0] Data_In_2,
  input  [31:0] Data_In_3,
  input  [3:0] Mask,
  input  nRead_Write,
  input  Chip_Select,
  input  Reset,
  output [31:0] Data_Out_0,
  output [31:0] Data_Out_1,
  output [31:0] Data_Out_2,
  output [31:0] Data_Out_3,
  output [3:0] Read_Time,
  output [3:0] Write_Time
);

  wire and_2_out, and_3_out, and_4_out, and_5_out, and_6_out, and_7_out, and_8_out, and_9_out, Changed, CLK,
       comparator_2_eq, comparator_3_eq, comparator_4_eq, comparator_5_eq, comparator_6_eq, Count,
       demultiplexer_3_out0, Idle, Idle_q, Load, Load0, Load1, nand_1_out, or_1_out, or_2_out, or_3_out,
       or_4_out, or_5_out, or_6_out, or_7_out, or_8_out, or_9_out, or_10_out, Proc_q, Update_Mem, Zero_Time;
  wire [3:0] counter_1_q, multiplexer_1_out, subtractor_1_out;
  wire [31:0] register_1_q, register_2_q, register_3_q, register_4_q, register_5_q;

  // Probe on 4'b0011
  // Probe on 4'b0010
  Multiplexer #(.width(4), .enable("false")) multiplexer_1 (
    .in0(4'b0011), .in1(4'b0010), .out(multiplexer_1_out), .sel(nRead_Write));
  or or_1 (or_1_out, Idle, Update_Mem);
  or or_2 (or_2_out, ~Chip_Select, Reset);  // OR_Gate
  Subtractor #(.width(4)) subtractor_1 (.a(multiplexer_1_out), .b(4'b0010), .out(subtractor_1_out));  // open: bin, bout
  D_Flip_Flop u_Idle (.clk(CLK), .D(or_1_out), .Q(Idle_q), .preset(or_2_out));  // open: Qn, en, reset
  Demultiplexer #(.enable("false")) demultiplexer_1 (.out0(Idle), .out1(Load0), .in(Idle_q), .sel(Changed));
  // Probe on counter_1_q
  Counter #(.width(4), .max('hf)) counter_1 (
    .load(Load), .D(subtractor_1_out), .count(Count), .Q(counter_1_q), .clk(CLK), .clr(or_3_out));  // open: carry
  or or_3 (or_3_out, ~Chip_Select, Reset);  // OR_Gate
  Comparator #(.width(4), .mode("unsigned")) comparator_1 (
    .a(4'b0000), .b(counter_1_q), .eq(Zero_Time));  // open: gt, lt
  or or_4 (or_4_out, Count, Load0, Load1);
  Register #(.width(32)) register_1 (.D(Data_In_0), .en(Chip_Select), .Q(register_1_q), .clk(CLK), .clr(or_5_out));
  or or_5 (or_5_out, ~Chip_Select, Reset);  // OR_Gate
  Register #(.width(32)) register_2 (.D(Data_In_1), .en(Chip_Select), .Q(register_2_q), .clk(CLK), .clr(or_6_out));
  or or_6 (or_6_out, ~Chip_Select, Reset);  // OR_Gate
  Register #(.width(32)) register_3 (.D(Data_In_2), .en(Chip_Select), .Q(register_3_q), .clk(CLK), .clr(or_7_out));
  or or_7 (or_7_out, ~Chip_Select, Reset);  // OR_Gate
  Register #(.width(32)) register_4 (.D(Data_In_3), .en(Chip_Select), .Q(register_4_q), .clk(CLK), .clr(or_8_out));
  or or_8 (or_8_out, ~Chip_Select, Reset);  // OR_Gate
  Register #(.width(32)) register_5 (
    .D({{11{1'b1}}, nRead_Write, Mask, Address}), .en(Chip_Select), .Q(register_5_q), .clk(CLK),
    .clr(or_9_out));
  or or_9 (or_9_out, ~Chip_Select, Reset);  // OR_Gate
  D_Flip_Flop Proc (.clk(CLK), .D(or_4_out), .Q(Proc_q), .reset(or_10_out));  // open: Qn, preset, en
  or or_10 (or_10_out, ~Chip_Select, Reset);  // OR_Gate
  Demultiplexer #(.enable("false")) demultiplexer_2 (
    .out0(Count), .out1(Update_Mem), .in(demultiplexer_3_out0), .sel(Zero_Time));
  Demultiplexer #(.enable("false")) demultiplexer_3 (
    .out0(demultiplexer_3_out0), .out1(Load1), .in(Proc_q), .sel(Changed));
  Clock clock_1 (.out(CLK));
  Comparator #(.width(32)) comparator_2 (.a(register_1_q), .b(Data_In_0), .eq(comparator_2_eq));  // open: gt, lt
  Comparator #(.width(32)) comparator_3 (.a(register_2_q), .b(Data_In_1), .eq(comparator_3_eq));  // open: gt, lt
  Comparator #(.width(32)) comparator_4 (.a(register_3_q), .b(Data_In_2), .eq(comparator_4_eq));  // open: gt, lt
  Comparator #(.width(32)) comparator_5 (.a(register_4_q), .b(Data_In_3), .eq(comparator_5_eq));  // open: gt, lt
  Comparator #(.width(32)) comparator_6 (
    .a(register_5_q), .b({{11{1'b1}}, nRead_Write, Mask, Address}), .eq(comparator_6_eq));  // open: gt, lt
  nand nand_1 (nand_1_out, comparator_6_eq, comparator_2_eq, comparator_3_eq, comparator_4_eq, comparator_5_eq);
  and and_1 (Changed, nand_1_out, Chip_Select);
  or or_11 (Load, Count, Load1, Load0);
  and and_2 (and_2_out, Mask[0], Update_Mem, nRead_Write);
  and and_3 (and_3_out, Mask[1], Update_Mem, nRead_Write);
  and and_4 (and_4_out, Mask[2], Update_Mem, nRead_Write);
  and and_5 (and_5_out, Mask[3], Update_Mem, nRead_Write);
  RAM_part #(.addrWidth(16), .dataWidth(32), .bus("separate")) ram_1 (
    .addr(Address), .din(Data_In_0), .data(Data_Out_0), .str(and_2_out), .sel(Chip_Select), .clk(CLK),
    .ld(and_6_out), .clr(Reset));
  and and_6 (and_6_out, ~nRead_Write, Idle);  // AND_Gate
  RAM_part #(.addrWidth(16), .dataWidth(32), .bus("separate")) ram_2 (
    .addr(Address), .din(Data_In_1), .data(Data_Out_1), .str(and_3_out), .sel(Chip_Select), .clk(CLK),
    .ld(and_7_out), .clr(Reset));
  and and_7 (and_7_out, ~nRead_Write, Idle);  // AND_Gate
  RAM_part #(.addrWidth(16), .dataWidth(32), .bus("separate")) ram_3 (
    .addr(Address), .din(Data_In_2), .data(Data_Out_2), .str(and_4_out), .sel(Chip_Select), .clk(CLK),
    .ld(and_8_out), .clr(Reset));
  and and_8 (and_8_out, ~nRead_Write, Idle);  // AND_Gate
  RAM_part #(.addrWidth(16), .dataWidth(32), .bus("separate")) ram_4 (
    .addr(Address), .din(Data_In_3), .data(Data_Out_3), .str(and_5_out), .sel(Chip_Select), .clk(CLK),
    .ld(and_9_out), .clr(Reset));
  and and_9 (and_9_out, ~nRead_Write, Idle);  // AND_Gate

  assign Read_Time = 4'b0011;
  assign Write_Time = 4'b0010;

  // Other names for the same wires on the sheet: M0 = Mask[0]; M1 = Mask[1]; M2 = Mask[2]; M3 = Mask[3];
  //   RW = nRead_Write; CLR = Reset; CS = Chip_Select; Load2 = Count

  // Notes on the sheet:
  //   NO MODIFICAR
  //   excepto quizás los valores RT y WT
  //   BANK0
  //   BANK1
  //   BANK2
  //   BANK3
endmodule

module S_MIPS (
  input  Kbd_Available,
  input  [6:0] Kbd_ASCII_Data,
  input  [31:0] RAM_Out_0,
  input  [31:0] RAM_Out_1,
  input  Reset,
  input  [31:0] RAM_Out_2,
  input  Clock,
  input  [31:0] RAM_Out_3,
  input  [3:0] Read_Time,
  input  [3:0] Write_Time,
  output Kbd_Enable,
  output [15:0] Address,
  output Kbd_Clear,
  output TTY_Enable,
  output [6:0] TTY_ASCII_Data,
  output Stop,
  output [31:0] RAM_In_0,
  output [31:0] RAM_In_1,
  output [31:0] RAM_In_2,
  output [31:0] RAM_In_3,
  output [3:0] Mask,
  output nRead_Write,
  output Chip_Select
);

  wire d_ff_1_q, Get_Data, Get_Inst, Inst_EN, PC_EN, Ready_Data, Ready_Inst, Ready_Write, Reg_EN, SP_EN,
       START, Start_EN, Write_Data;
  wire [5:0] Func_Code, OP_Code;
  wire [31:0] bit_extender_1_out, DP_Addres, Inst, multiplexer_1_out;

  Control_Unit control_unit_1 (
    .in_1(START), .in_2(Clock), .in_3(Reset), .in_4(Ready_Inst), .in_5(Ready_Data), .in_6(Ready_Write),
    .in_7(OP_Code), .in_8(Func_Code), .Get_Inst(Get_Inst), .PCen(PC_EN), .SPen(SP_EN), .INSTen(Inst_EN),
    .KBDen(Kbd_Enable), .RegW(Reg_EN), .TTYen(TTY_Enable), .WriteD(Write_Data), .startEN(Start_EN),
    .Get_Data(Get_Data), .End(Stop));
  Multiplexer #(.width(32)) multiplexer_1 (
    .in0({32{1'b1}}), .in1(bit_extender_1_out), .out(multiplexer_1_out), .sel(Kbd_Available));  // open: en
  assign bit_extender_1_out = {{25{1'b0}}, Kbd_ASCII_Data};  // Bit_Extender bit_extender_1
  D_Flip_Flop #(.trigger("falling")) d_ff_1 (
    .clk(Clock), .D(1'b0), .Q(d_ff_1_q), .preset(Reset));  // open: Qn, en, reset
  D_Flip_Flop #(.trigger("falling")) d_ff_2 (
    .clk(Clock), .D(d_ff_1_q), .Q(START), .reset(Reset));  // open: Qn, preset, en
  Data_Path data_path_1 (
    .Inst(Inst), .KBD(multiplexer_1_out), .ID_EN(Inst_EN), .PC_EN(PC_EN), .KBD_EN(Kbd_Enable), .SP_EN(SP_EN),
    .Start(Start_EN), .Reset(Reset), .Read_Write(Reg_EN), .Clk(Clock), .Address(DP_Addres),
    .Data_Ram(RAM_In_0), .tty(TTY_ASCII_Data), .OP_Code(OP_Code), .Func_Code(Func_Code));
  Access access_1 (
    .in_1(DP_Addres), .in_2(RAM_Out_0), .in_3(RAM_Out_1), .in_4(RAM_Out_2), .in_5(RAM_Out_3),
    .in_6(Read_Time), .in_7(Write_Time), .in_8(Write_Data), .in_9(Clock), .in_10(Reset), .in_11(Get_Inst),
    .in_12(Get_Data), .in_13(Inst_EN), .Mask(Mask), .RAM_OUT(Inst), .RW(nRead_Write),
    .Chip_Select(Chip_Select), .Ready_Inst(Ready_Inst), .Address(Address), .Ready_Data(Ready_Data),
    .Ready_write(Ready_Write));

  assign Kbd_Clear = Reset;
  assign RAM_In_1 = RAM_In_0;
  assign RAM_In_2 = RAM_In_0;
  assign RAM_In_3 = RAM_In_0;

  // Other names for the same wires on the sheet: CLK = Clock; CS = Chip_Select; KBD_AVAIL = Kbd_Available;
  //   CLR = Reset; KBD_CLR = Reset; KBD_DATA[6:0] = Kbd_ASCII_Data; RAM_A[15:0] = Address; Data_RAM[31:0] = RAM_In_0;
  //   RAM_INPUT_0[31:0] = RAM_In_0; RAM_INPUT_1[31:0] = RAM_In_0; RAM_INPUT_2[31:0] = RAM_In_0;
  //   RAM_INPUT_3[31:0] = RAM_In_0; RAM_MASK[3:0] = Mask; RAM_OUTPUT_0[31:0] = RAM_Out_0;
  //   RAM_OUTPUT_1[31:0] = RAM_Out_1; RAM_OUTPUT_2[31:0] = RAM_Out_2; RAM_OUTPUT_3[31:0] = RAM_Out_3;
  //   RW = nRead_Write; TTY_DATA[6:0] = TTY_ASCII_Data

  // Notes on the sheet:
  //   RAM ADDRESS
  //   DATA FROM RAM
  //   DATA TO RAM
  //   DATA WRITE MASK
  //   RAM TIMING
  //   RAM CONTROL
  //   KEYBOARD
  //   TTY
  //   SEQUENCING
endmodule

module RAM_Dispatcher (
  input  [3:0] WriteTime,
  input  Clock,
  input  CLR,
  output [31:0] Data,
  output [15:0] Address,
  output [3:0] Mask,
  output Finished,
  output Write
);

  wire demultiplexer_2_out1, demultiplexer_3_out1, End, IDLE_q, IncAddr, Load, or_1_out, or_2_out, While_q,
       WriteEnd;
  wire [3:0] counter_1_q;
  wire [31:0] CurrentAddress_q;

  Counter #(.width(32), .max('hffffffff)) CurrentAddress (
    .count(IncAddr), .Q({CurrentAddress_q[31:18], Address, CurrentAddress_q[1:0]}), .clk(Clock), .clr(CLR));  // open: load, D, carry
  or or_1 (or_1_out, IncAddr, demultiplexer_3_out1, Finished);
  D_Flip_Flop IDLE (.clk(Clock), .D(or_1_out), .Q(IDLE_q), .preset(CLR));  // open: Qn, en, reset
  Demultiplexer #(.enable("false")) demultiplexer_1 (.out0(Load), .out1(Finished), .in(IDLE_q), .sel(End));
  D_Flip_Flop While (.clk(Clock), .D(or_2_out), .Q(While_q), .reset(CLR));  // open: Qn, preset, en
  or or_2 (or_2_out, Write, Load);
  RAM_part #(.addrWidth(18), .dataWidth(32)) ram_1 (
    .addr({Address, CurrentAddress_q[1:0]}), .data(Data), .clk(Clock));  // open: sel, ld, clr
  Demultiplexer #(.enable("false")) demultiplexer_2 (
    .out0(Write), .out1(demultiplexer_2_out1), .in(While_q), .sel(WriteEnd));
  Decoder #(.select(2)) decoder_1 (
    .out0(Mask[0]), .out1(Mask[1]), .out2(Mask[2]), .out3(Mask[3]), .sel(CurrentAddress_q[1:0]));  // open: en
  Demultiplexer #(.enable("false")) demultiplexer_3 (
    .out0(IncAddr), .out1(demultiplexer_3_out1), .in(demultiplexer_2_out1), .sel(End));
  Counter #(.width(4), .max('hf)) counter_1 (
    .load(Load), .D(WriteTime), .count(Write), .Q(counter_1_q), .clk(Clock));  // open: carry, clr
  Comparator #(.width(32)) comparator_1 (.a(Data), .b({32{1'b1}}), .eq(End));  // open: gt, lt
  Comparator #(.width(4)) comparator_2 (.a(4'b0000), .b(counter_1_q), .eq(WriteEnd));  // open: gt, lt

  // Other names for the same wires on the sheet: CLK = Clock; Count = Write; WT[3:0] = WriteTime
endmodule

module Data_Path (
  input  [31:0] Inst,
  input  [31:0] KBD,
  input  ID_EN,
  input  PC_EN,
  input  KBD_EN,
  input  SP_EN,
  input  Start,
  input  Reset,
  input  Read_Write,
  input  Clk,
  output [31:0] Address,
  output [31:0] Data_Ram,
  output [6:0] tty,
  output [5:0] OP_Code,
  output [5:0] Func_Code
);

  wire alu_1_out_10, and_1_out, halt, I, J, kbd_t, lw, mfhi, mflo, pop, push, R, rnd, sw, tty_t;
  wire [4:0] multiplexer_2_out, Rd, Rs, Rt;
  wire [15:0] Const;
  wire [25:0] Jump;
  wire [31:0] A, B, HI, LO, multiplexer_1_out, multiplexer_3_out, PC, PC_prime, QHI, QLO, Res, SP;

  Branch_Control branch_control_1 (
    .PC(PC), .Rs(A), .Rt(B), .Jump(Jump), .Offset(Const), .Func_Code(Func_Code), .Op_Code(OP_Code),
    .Next_inst(PC_prime));
  Instruction_Decoder instruction_decoder_1 (
    .Inst(Inst), .Clock(Clk), .Reset(Reset), .Enable(ID_EN), .Jump(Jump), .Operation_Code(OP_Code),
    .Constant_Offset(Const), .Function_Code(Func_Code), .Rd(Rd), .Rt(Rt), .Rs(Rs));
  OP_Identifier op_identifier_1 (.OP_Code(OP_Code), .J(J), .R(R), .I(I));
  Program_Counter program_counter_1 (.out_5(PC_prime), .Clock(Clk), .Reset(Reset), .Enable(PC_EN), .in_1(PC));
  and and_1 (and_1_out, pop, lw);
  Multiplexer #(.width(32)) multiplexer_1 (
    .in0(Res), .in1(Inst), .out(multiplexer_1_out), .sel(and_1_out));  // open: en
  Multiplexer #(.width(5)) multiplexer_2 (.in0(Rd), .in1(Rt), .out(multiplexer_2_out), .sel(I));  // open: en
  Other_OP_Decoder other_op_decoder_1 (
    .OP_Code(OP_Code), .Func_Code(Func_Code), .Start(Start), .mfhi(mfhi), .mflo(mflo), .pop(pop),
    .push(push), .lw(lw), .sw(sw), .tty(tty_t), .rnd(rnd), .kbd(kbd_t), .halt(halt));
  Multiplexer #(.width(32)) multiplexer_3 (
    .in0(multiplexer_1_out), .in1(KBD), .out(multiplexer_3_out), .sel(KBD_EN));  // open: en
  ALU alu_1 (
    .in_1(A), .in_2(B), .in_3(Func_Code), .in_4(OP_Code), .in_5(Const), .Tipo_de_Instruccion(I),
    .Output(Res), .Hi(HI), .LO(LO), .out_10(alu_1_out_10));
  Multiplexer #(.width(32)) multiplexer_4 (
    .in0(A), .in1(B), .out({Data_Ram[7:0], Data_Ram[15:8], Data_Ram[23:16], Data_Ram[31:24]}), .sel(sw));  // open: en
  File file_1 (
    .in_1(multiplexer_3_out), .in_2(HI), .in_3(LO), .in_4(multiplexer_2_out), .in_5(Rs), .in_6(Rt),
    .in_7(Read_Write), .in_8(SP_EN), .out_17(QHI), .out_18(SP), .Output(A), .out_20(B), .in_9(Reset),
    .in_10(rnd), .in_11(Clk), .in_12(mfhi), .out_21(QLO), .in_13(alu_1_out_10), .in_14(mflo), .in_15(push),
    .in_16(pop));
  Memory_Address memory_address_1 (.PC(PC), .SP(SP), .F(Res), .push(push), .pop(pop), .lw(lw), .sw(sw), .out(Address));
  Bit_Extender #(.in_width(32), .out_width(7)) bit_extender_1 (.in(A), .out(tty));

  // Other names for the same wires on the sheet: Func[5:0] = Func_Code; OP[5:0] = OP_Code; R_W = Read_Write
endmodule

module Program_Counter (
  input  [31:0] in_1,
  input  Clock,
  input  Reset,
  input  Enable,
  output [31:0] out_5
);

  Register #(.width(32)) register_1 (.D(out_5), .en(Enable), .Q(in_1), .clk(Clock), .clr(Reset));
endmodule

// Inst-Dec
module Instruction_Decoder (
  input  [31:0] Inst,
  input  Clock,
  input  Reset,
  input  Enable,
  output [25:0] Jump,
  output [5:0] Operation_Code,
  output [15:0] Constant_Offset,
  output [5:0] Function_Code,
  output [4:0] Rd,
  output [4:0] Rt,
  output [4:0] Rs
);

  Register #(.width(32)) register_1 (
    .D(Inst), .en(Enable), .Q({Operation_Code, Jump[25:16], Constant_Offset}), .clk(Clock), .clr(Reset));

  assign Function_Code = Constant_Offset[5:0];
  assign Jump[15:0] = Constant_Offset;
  assign Rd = Constant_Offset[15:11];
  assign Rs = Jump[25:21];
  assign Rt = Jump[20:16];

  // Other names for the same wires on the sheet: Func_Code[5:0] = Constant_Offset[5:0];
  //   nn[25:0] = {Jump[25:16], Constant_Offset}; OP_Code[5:0] = Operation_Code
endmodule

// OP_ID
module OP_Identifier (
  input  [5:0] OP_Code,
  output J,
  output R,
  output I
);

  wire comparator_2_eq, comparator_3_eq, comparator_4_eq;

  Comparator #(.width(6)) comparator_1 (.a(OP_Code), .b(6'b000010), .eq(J));  // open: gt, lt
  Comparator #(.width(6)) comparator_2 (.a(OP_Code), .b({6{1'b0}}), .eq(comparator_2_eq));  // open: gt, lt
  Comparator #(.width(6)) comparator_3 (.a(OP_Code), .b({6{1'b1}}), .eq(comparator_3_eq));  // open: gt, lt
  Comparator #(.width(6)) comparator_4 (.a(OP_Code), .b(6'b111000), .eq(comparator_4_eq));  // open: gt, lt
  or or_1 (R, comparator_2_eq, comparator_3_eq, comparator_4_eq);
  and and_1 (I, R, J);
endmodule

// O_OP _Dec
module Other_OP_Decoder (
  input  [5:0] OP_Code,
  input  [5:0] Func_Code,
  input  Start,
  output mfhi,
  output mflo,
  output pop,
  output push,
  output lw,
  output sw,
  output tty,
  output rnd,
  output kbd,
  output halt
);

  wire and_1_out, and_2_out, and_3_out, and_4_out, and_5_out, and_6_out, and_7_out, and_8_out,
       comparator_1_eq, comparator_2_eq, comparator_3_eq, comparator_4_eq, comparator_5_eq, comparator_6_eq,
       comparator_7_eq, comparator_8_eq, comparator_9_eq, comparator_10_eq, comparator_11_eq,
       comparator_12_eq, comparator_13_eq;

  Comparator #(.width(6)) comparator_1 (.a(OP_Code), .b({6{1'b0}}), .eq(comparator_1_eq));  // open: gt, lt
  Comparator #(.width(6)) comparator_2 (.a(Func_Code), .b(6'b010000), .eq(comparator_2_eq));  // open: gt, lt
  Comparator #(.width(6)) comparator_3 (.a(Func_Code), .b(6'b010010), .eq(comparator_3_eq));  // open: gt, lt
  Comparator #(.width(6)) comparator_4 (.a(OP_Code), .b(6'b111000), .eq(comparator_4_eq));  // open: gt, lt
  Comparator #(.width(6)) comparator_5 (.a(Func_Code), .b({6{1'b0}}), .eq(comparator_5_eq));  // open: gt, lt
  Comparator #(.width(6)) comparator_6 (.a(Func_Code), .b(6'b000001), .eq(comparator_6_eq));  // open: gt, lt
  Comparator #(.width(6)) comparator_7 (.a(OP_Code), .b(6'b100011), .eq(comparator_7_eq));  // open: gt, lt
  Comparator #(.width(6)) comparator_8 (.a(OP_Code), .b(6'b101011), .eq(comparator_8_eq));  // open: gt, lt
  Comparator #(.width(6)) comparator_9 (.a(OP_Code), .b({6{1'b1}}), .eq(comparator_9_eq));  // open: gt, lt
  Comparator #(.width(6)) comparator_10 (.a(Func_Code), .b(6'b000001), .eq(comparator_10_eq));  // open: gt, lt
  Comparator #(.width(6)) comparator_11 (.a(Func_Code), .b(6'b000010), .eq(comparator_11_eq));  // open: gt, lt
  Comparator #(.width(6)) comparator_12 (.a(Func_Code), .b(6'b000100), .eq(comparator_12_eq));  // open: gt, lt
  Comparator #(.width(6)) comparator_13 (.a(Func_Code), .b({6{1'b1}}), .eq(comparator_13_eq));  // open: gt, lt
  and and_1 (and_1_out, comparator_1_eq, comparator_2_eq);
  and and_2 (and_2_out, comparator_1_eq, comparator_3_eq);
  and and_3 (and_3_out, comparator_4_eq, comparator_5_eq);
  and and_4 (and_4_out, comparator_4_eq, comparator_6_eq);
  and and_5 (and_5_out, comparator_9_eq, comparator_10_eq);
  and and_6 (and_6_out, comparator_9_eq, comparator_11_eq);
  and and_7 (and_7_out, comparator_9_eq, comparator_12_eq);
  and and_8 (and_8_out, comparator_9_eq, comparator_13_eq);
  and and_9 (mfhi, Start, and_1_out);
  and and_10 (mflo, Start, and_2_out);
  and and_11 (pop, Start, and_3_out);
  and and_12 (push, Start, and_4_out);
  and and_13 (lw, Start, comparator_7_eq);
  and and_14 (sw, Start, comparator_8_eq);
  and and_15 (tty, Start, and_5_out);
  and and_16 (rnd, Start, and_6_out);
  and and_17 (kbd, Start, and_7_out);
  and and_18 (halt, Start, and_8_out);
endmodule

module Branch_Control (
  input  [31:0] PC,
  input  [31:0] Rs,
  input  [31:0] Rt,
  input  [25:0] Jump,
  input  [15:0] Offset,
  input  [5:0] Func_Code,
  input  [5:0] Op_Code,
  output [31:0] Next_inst
);

  wire and_1_out, and_2_out, and_3_out, and_4_out, and_5_out, beq, bgtz, blez, bltz, bne, Comp,
       comparator_1_eq, comparator_2_gt, comparator_2_lt, j, jr;
  wire [31:0] adder_1_out, adder_2_out, multiplexer_1_out, multiplexer_2_out;
  wire [31:17] PC_Offset;

  Comparator #(.width(32)) comparator_1 (.a(Rs), .b(Rt), .eq(comparator_1_eq));  // open: gt, lt
  Comparator #(.width(32)) comparator_2 (
    .a(Rs), .b({32{1'b0}}), .gt(comparator_2_gt), .lt(comparator_2_lt));  // open: eq
  Adder #(.width(32)) adder_1 (.a(PC), .b(32'h4), .out(adder_1_out));  // open: cin, cout
  Multiplexer #(.width(32)) multiplexer_1 (
    .in0({32{1'b0}}), .in1({PC_Offset, Offset[14:0], 2'b00}), .out(multiplexer_1_out), .sel(Comp));  // open: en
  and and_1 (and_1_out, beq, comparator_1_eq);
  and and_2 (and_2_out, ~comparator_1_eq, bne);  // AND_Gate
  and and_3 (and_3_out, ~comparator_2_gt, blez);  // AND_Gate
  and and_4 (and_4_out, comparator_2_gt, bgtz);
  and and_5 (and_5_out, comparator_2_lt, bltz);
  Adder #(.width(32)) adder_2 (.a(adder_1_out), .b(multiplexer_1_out), .out(adder_2_out));  // open: cin, cout
  assign PC_Offset = {{14{Offset[15]}}, Offset[15]};  // Bit_Extender bit_extender_1
  Multiplexer #(.width(32)) multiplexer_2 (
    .in0(adder_2_out), .in1({PC[31:28], Jump, 2'b00}), .out(multiplexer_2_out), .sel(j));  // open: en
  or or_1 (Comp, and_1_out, and_2_out, and_3_out, and_4_out, and_5_out);
  Multiplexer #(.width(32)) multiplexer_3 (.in0(multiplexer_2_out), .in1(Rs), .out(Next_inst), .sel(jr));  // open: en
  Jump_Control jump_control_1 (
    .Func_Code(Func_Code), .Op_Code(Op_Code), .jr(jr), .bltz(bltz), .j(j), .beq(beq), .bne(bne), .blez(blez),
    .bgtz(bgtz));

  // Other names for the same wires on the sheet: PC_Jump[31:2] = {PC[31:28], Jump}; PC_Offset[16:2] = Offset[14:0];
  //   PC_Out[31:0] = Next_inst
endmodule

module Jump_Control (
  input  [5:0] Func_Code,
  input  [5:0] Op_Code,
  output jr,
  output bltz,
  output j,
  output beq,
  output bne,
  output blez,
  output bgtz
);

  wire comparator_1_eq, comparator_2_eq;

  Comparator #(.width(6)) comparator_1 (.a(Op_Code), .b({6{1'b0}}), .eq(comparator_1_eq));  // open: gt, lt
  Comparator #(.width(6)) comparator_2 (.a(Func_Code), .b(6'b001000), .eq(comparator_2_eq));  // open: gt, lt
  Comparator #(.width(6)) comparator_3 (.a(Op_Code), .b(6'b000001), .eq(bltz));  // open: gt, lt
  Comparator #(.width(6)) comparator_4 (.a(Op_Code), .b(6'b000010), .eq(j));  // open: gt, lt
  Comparator #(.width(6)) comparator_5 (.a(Op_Code), .b(6'b000100), .eq(beq));  // open: gt, lt
  Comparator #(.width(6)) comparator_6 (.a(Op_Code), .b(6'b000101), .eq(bne));  // open: gt, lt
  Comparator #(.width(6)) comparator_7 (.a(Op_Code), .b(6'b000110), .eq(blez));  // open: gt, lt
  Comparator #(.width(6)) comparator_8 (.a(Op_Code), .b(6'b000111), .eq(bgtz));  // open: gt, lt
  and and_1 (jr, comparator_1_eq, comparator_2_eq);

  // Other names for the same wires on the sheet: Op_Codee[5:0] = Op_Code
endmodule

// Address
module Memory_Address (
  input  [31:0] PC,
  input  [31:0] SP,
  input  [31:0] F,
  input  push,
  input  pop,
  input  lw,
  input  sw,
  output [31:0] out
);

  wire or_1_out, or_2_out;
  wire [31:0] multiplexer_1_out;

  or or_1 (or_1_out, pop, push);
  Multiplexer #(.width(32)) multiplexer_1 (.in0(PC), .in1(SP), .out(multiplexer_1_out), .sel(or_1_out));  // open: en
  Multiplexer #(.width(32)) multiplexer_2 (.in0(multiplexer_1_out), .in1(F), .out(out), .sel(or_2_out));  // open: en
  or or_2 (or_2_out, lw, sw);
endmodule

module Control_Unit (
  input  in_1,
  input  in_2,
  input  in_3,
  input  in_4,
  input  in_5,
  input  in_6,
  input  [5:0] in_7,
  input  [5:0] in_8,
  output Get_Inst,
  output PCen,
  output SPen,
  output INSTen,
  output KBDen,
  output RegW,
  output TTYen,
  output WriteD,
  output startEN,
  output Get_Data,
  output End
);

  wire ALU, and_1_out, and_2_out, and_3_out, and_5_out, Copy, d_ff_1_q, d_ff_5_q, d_ff_6_q, d_ff_8_q,
       d_ff_9_q, demultiplexer_1_out0, demultiplexer_2_out0, demultiplexer_3_out0, demultiplexer_4_out0,
       demultiplexer_4_out1, halt, Jump, kbd, lw, Memory, or_1_out, or_2_out, or_3_out, or_5_out, pop, push,
       \rand , SP_1, SP_2, Specials, startEN_t, sw, tty;

  D_Flip_Flop #(.trigger("falling")) d_ff_1 (
    .clk(in_2), .D(Memory), .Q(d_ff_1_q), .reset(in_3));  // open: Qn, preset, en
  or or_1 (or_1_out, End, and_1_out);
  and and_1 (and_1_out, Specials, halt);
  and and_2 (and_2_out, Specials, \rand );
  and and_3 (and_3_out, Specials, kbd);
  Demultiplexer #(.enable("false")) demultiplexer_1 (
    .out0(demultiplexer_1_out0), .out1(Get_Data), .in(d_ff_1_q), .sel(or_2_out));
  or or_2 (or_2_out, lw, pop);
  D_Flip_Flop #(.trigger("falling")) d_ff_2 (.clk(in_2), .D(or_1_out), .Q(End), .reset(in_3));  // open: Qn, preset, en
  Demultiplexer #(.enable("false")) demultiplexer_2 (
    .out0(demultiplexer_2_out0), .out1(SP_1), .in(demultiplexer_1_out0), .sel(push));
  or or_3 (or_3_out, ALU, Copy, and_2_out, and_3_out, in_5);
  Operations operations_1 (
    .in_1(in_8), .in_2(in_7), .EN(startEN_t), .ALU(ALU), .Copy(Copy), .Jump(Jump), .Memory(Memory),
    .Specials(Specials));
  D_Flip_Flop #(.trigger("falling")) d_ff_3 (.clk(in_2), .D(or_3_out), .Q(RegW));  // open: Qn, preset, en, reset
  D_Flip_Flop #(.trigger("falling")) d_ff_4 (
    .clk(in_2), .D(in_4), .Q(startEN_t), .reset(in_3));  // open: Qn, preset, en
  D_Flip_Flop #(.trigger("falling")) d_ff_5 (.clk(in_2), .D(RegW), .Q(d_ff_5_q), .reset(in_3));  // open: Qn, preset, en
  D_Flip_Flop #(.trigger("falling")) d_ff_6 (.clk(in_2), .D(SP_1), .Q(d_ff_6_q), .reset(in_3));  // open: Qn, preset, en
  Demultiplexer #(.enable("false")) demultiplexer_3 (
    .out0(demultiplexer_3_out0), .out1(SP_2), .in(d_ff_5_q), .sel(pop));
  D_Flip_Flop #(.trigger("falling")) d_ff_7 (
    .clk(in_2), .Q(startEN), .preset(startEN_t), .reset(PCen));  // open: D, Qn, en
  or or_4 (WriteD, demultiplexer_2_out0, d_ff_6_q);
  and and_4 (KBDen, kbd, demultiplexer_3_out0);
  D_Flip_Flop #(.trigger("falling")) d_ff_8 (.clk(in_2), .D(SP_2), .Q(d_ff_8_q), .reset(in_3));  // open: Qn, preset, en
  Other_OP_Decoder other_op_decoder_1 (
    .OP_Code(in_7), .Func_Code(in_8), .Start(1'b1), .pop(pop), .push(push), .lw(lw), .sw(sw), .tty(tty),
    .rnd(\rand ), .kbd(kbd), .halt(halt));  // open: mfhi, mflo
  D_Flip_Flop #(.trigger("falling")) d_ff_9 (
    .clk(in_2), .D(demultiplexer_4_out0), .Q(d_ff_9_q), .preset(in_3));  // open: Qn, en, reset
  and and_5 (and_5_out, Specials, tty);
  Demultiplexer #(.enable("false")) demultiplexer_4 (
    .out0(demultiplexer_4_out0), .out1(demultiplexer_4_out1), .in(d_ff_9_q), .sel(in_1));
  or or_5 (or_5_out, demultiplexer_3_out0, in_6, Jump, and_5_out, d_ff_8_q);
  or or_6 (Get_Inst, demultiplexer_4_out1, PCen);
  D_Flip_Flop #(.trigger("falling")) IDLE (.clk(in_2), .D(or_5_out), .Q(PCen), .reset(in_3));  // open: Qn, preset, en
  or or_7 (SPen, SP_1, SP_2);
  and and_6 (TTYen, Specials, tty, startEN);

  assign INSTen = in_4;

  // Other names for the same wires on the sheet: CLK = in_2; En = startEN; F_Code[5:0] = in_8; kbd_EN = KBDen;
  //   Op_code[5:0] = in_7; Ready_Data = in_5; Inst_EN = in_4; Ready_Inst = in_4; Ready_Write = in_6; RegEN = RegW;
  //   Res = in_3; START = in_1; stopEN = PCen; Write_Data = WriteD
endmodule
